# Fritzing sketch interphone (saved by Fritzing 0.9.3b)
perfboards: 1

parts:
  R1 = Resistor [tolerance=±5% resistance=1k package=THT]
  Q1 = NPN-Transistor [package="TO92 [THT]"]
  Stabilisation_GPIO2 = Electrolytic Capacitor [capacitance=0.47mF package="100 mil [THT, electrolytic]"]
  Q2 = NPN-Transistor [package="TO92 [THT]"]
  R2 = Resistor [tolerance=±5% resistance=10k package=THT]
  R3 = Resistor [tolerance=±5% resistance=10k package=THT]
  R4 = Resistor [tolerance=±5% resistance=1k package=THT]
  R5 = Resistor [tolerance=±5% resistance=1k package=THT]
  K1 = Relay [part_number=FRS1B-S package=THT]
  R6 = Resistor [tolerance=±5% resistance=1k package=THT]
  D1 = Rectifier Diode [part_number=1N4001 package="300 mil [THT]"]
  R7 = Resistor [tolerance=±2% resistance=2.0k package=THT]
  LED1 = LED - 5mm [color="Red (633nm)" package="5 mm [THT]"]
  RX = male pin header, 1 pin [form="♂ (male)"]
  TX = male pin header, 1 pin [form="♂ (male)"]
  Tampon_ESP = Electrolytic Capacitor [capacitance=0.1mF package="100 mil [THT, electrolytic]"]
  Flash = male pin header, 1 pin [form="♂ (male)"]
  Normal = male pin header, 1 pin [form="♂ (male)"]
  Mode = male pin header, 1 pin [form="♂ (male)"]  # not connected
  Interphone_1 = male pin header, 1 pin [form="♂ (male)"]
  Interphone_2 = male pin header, 1 pin [form="♂ (male)"]
  part = ESP8266 WiFi Module [part_number=ESP8266]

nets:
  N1: R1.Pin_0, R2.Pin_0, R3.Pin_1, D1.cathode, R7.Pin_0, Tampon_ESP.+, Normal.pin1, part.VCC
  N2: R1.Pin_1, part.CH_PD
  N3: Q1.E, Q2.C
  N4: Q1.B, R6.Pin_0
  N5: Q1.C, K1.COIL2, LED1.anode
  N6: Stabilisation_GPIO2.-, Q2.E, Tampon_ESP.-, Flash.pin1, part.GND
  N7: Stabilisation_GPIO2.+, R3.Pin_0, R5.Pin_1
  N8: Q2.B, R5.Pin_0
  N9: R2.Pin_1, part.RST
  N10: R4.Pin_0, part.GPIO_0
  N11: K1.A, Interphone_1.pin1
  N12: K1.COIL1, D1.anode
  N13: K1.C1, K1.C2, Interphone_2.pin1
  N14: R6.Pin_1, part.GPIO_2
  N15: R7.Pin_1, LED1.cathode
  N16: RX.pin1, part.RXD
  N17: TX.pin1, part.TXD

custom parts:
  ESP8266 WiFi Module: Generic WiFi Module based on the ESP8266 with onboard PCB antenna and UART communications
